// Logisim project D flip flop using AND , NOR.circ as structural Verilog: 1 circuit, main circuit main
module main (
  input  D,
  input  E,
  output Q1,
  output Q2
);

  wire and_1_out, and_2_out, not_1_out;

  not not_1 (not_1_out, D);
  and and_1 (and_1_out, D, E);
  and and_2 (and_2_out, not_1_out, E);
  nor nor_1 (Q1, and_1_out, Q2);
  nor nor_2 (Q2, Q1, and_2_out);
endmodule
