// Logisim project JK flipflop.circ as structural Verilog: 1 circuit, main circuit main
module main (
  input  J,
  input  K
);

  wire and_1_out, and_2_out, clock_1_out, d_ff_1_q, not_1_out, not_2_out, or_1_out;

  not not_1 (not_1_out, K);
  and and_1 (and_1_out, J, not_2_out);
  and and_2 (and_2_out, not_1_out, d_ff_1_q);
  or or_1 (or_1_out, and_1_out, and_2_out);
  Clock clock_1 (.out(clock_1_out));
  not not_2 (not_2_out, d_ff_1_q);
  D_Flip_Flop d_ff_1 (.clk(clock_1_out), .D(or_1_out), .Q(d_ff_1_q));  // open: Qn, preset, en, reset
endmodule
