// Logisim project T flip flop.circ as structural Verilog: 1 circuit, main circuit main
module main (
  input  T,
  output out_2
);

  wire clock_1_out, xor_1_out;

  xor xor_1 (xor_1_out, T, out_2);
  Clock clock_1 (.out(clock_1_out));
  D_Flip_Flop d_ff_1 (.clk(clock_1_out), .D(xor_1_out), .Q(out_2));  // open: Qn, preset, en, reset
endmodule
