// Logisim project XOR DATA ERROR DETECTION_PROJ.circ as structural Verilog: 1 circuit, main circuit main
module main (
  input  ORIGINAL_INPUT,
  input  in_2,
  input  in_3,
  input  in_4,
  input  in_5,
  input  in_6,
  input  in_7,
  input  in_8
);

  wire not_1_out, or_1_out, xor_1_out, xor_2_out, xor_3_out, xor_4_out;

  xor xor_1 (xor_1_out, ORIGINAL_INPUT, in_5);
  xor xor_2 (xor_2_out, in_2, in_6);
  xor xor_3 (xor_3_out, in_3, in_7);
  xor xor_4 (xor_4_out, in_4, in_8);
  LED led_1 (.in(not_1_out));
  not not_1 (not_1_out, or_1_out);
  or or_1 (or_1_out, xor_1_out, xor_2_out, xor_3_out, xor_4_out);
  LED led_2 (.in(or_1_out));

  // Other names for the same wires on the sheet: i1 = ORIGINAL_INPUT; i2 = in_2; i3 = in_3; i4 = in_4; R1 = in_5;
  //   R2 = in_6; R3 = in_7; R4 = in_8

  // Notes on the sheet:
  //   RECIEVED DATA
  //   NO ERROR
  //   ERROR DETECTED
endmodule
